# Fritzing sketch layout (saved by Fritzing 0.9.2b)
breadboards: 1

parts:
  Part1 = Arduino Uno (Rev3)
  RaspberryPi1 = Raspberry Pi Model B
  Part2 = Coin Acceptor - 6-Coin version
  RFID1 = RFID Reader [package="DIP (Dual Inline) [THT]"]
  R1 = Resistor [tolerance=±5% resistance=10k package="0402 [SMD]"]
  R2 = Resistor [tolerance=±5% resistance=30k package="0402 [SMD]"]

nets:
  GND: Part1.GND, RaspberryPi1.GND, Part2.GND, RFID1.GND, R2.Pin_0
  N1: Part1.D5_PWM, RFID1.D0
  N2: Part1.D6_PWM, RFID1.D1
  N3: RaspberryPi1.RXD, R1.Pin_0, R2.Pin_1
  N4: RaspberryPi1.#18, Part2.INH
  N5: Part2.SIG, R1.Pin_1
  12V: Part2.12V, RFID1.12V

notes:
  Arduino to Pi is currently serial over USB. Arduino gets powered by this connection.
  DIP: 0011
  Voltage rail is +12V

custom parts:
  Raspberry Pi Model B: Raspberry Pi (Model B)
  Coin Acceptor - 6-Coin version: 12V coin acceptor that can handle up to 6 different denominations. Output is either pulse width, serial, or single pin per coin value.
  RFID Reader: RFID reader
